// Logisim project 8bit computer.circ as structural Verilog: 5 circuits, main circuit main
module main (
  input  in_1
);

  wire and_1_out, and_2_out, and_3_out, and_4_out, and_5_out, and_6_out, binary_to_bcd_1_negative,
       clock_1_out, comparator_1_eq, comparator_1_gt, comparator_1_lt, d_ff_1_q, not_1_out, not_2_out,
       not_3_out, not_4_out, not_5_out, not_6_out, or_1_out, or_2_out, or_3_out, pull_resistor_2_node,
       pull_resistor_4_node, ram_select_1_en, ram_select_1_s0, ram_select_1_s1, step_reset_1_out_2;
  wire [2:0] counter_1_q;
  wire [3:0] binary_to_bcd_1_hundreds, binary_to_bcd_1_tens, binary_to_bcd_1_units, controlled_buffer_3_out,
       controlled_buffer_8_out, I_q, MA_q, PC_q, pull_resistor_1_node;
  wire [6:3] I_q_2;
  wire [7:0] A_q, adder_1_out, B_q, controlled_buffer_4_out, controlled_buffer_5_out,
       controlled_buffer_10_out, controlled_buffer_12_out, controlled_buffer_13_out,
       controlled_inverter_1_out, OUT_q, pull_resistor_3_node, SUM_q;
  wire [16:0] rom_1_data;

  LED led_1 (.in(pull_resistor_1_node[3]));
  LED led_2 (.in(pull_resistor_1_node[2]));
  LED led_3 (.in(pull_resistor_1_node[1]));
  LED led_4 (.in(I_q_2[4]));
  LED led_5 (.in(I_q_2[6]));
  LED led_6 (.in(I_q_2[5]));
  not not_1 (not_1_out, and_6_out);
  and and_1 (and_1_out, comparator_1_eq, I_q_2[4]);
  and and_2 (and_2_out, comparator_1_lt, I_q_2[5]);
  or or_1 (or_1_out, and_2_out, and_1_out, and_3_out);
  Pull_Resistor pull_resistor_1 (.node(pull_resistor_1_node));
  LED led_7 (.in(pull_resistor_3_node[7]));
  LED led_8 (.in(pull_resistor_1_node[0]));
  LED led_9 (.in(pull_resistor_3_node[6]));
  LED led_10 (.in(I_q[2]));
  LED led_11 (.in(I_q[1]));
  LED led_12 (.in(I_q_2[3]));
  LED led_13 (.in(I_q[3]));
  LED led_14 (.in(counter_1_q[2]));
  LED led_15 (.in(counter_1_q[1]));
  Counter #(.width(3), .max('h7)) counter_1 (
    .Q(counter_1_q), .clk(not_1_out), .clr(step_reset_1_out_2));  // open: load, D, count, carry
  and and_3 (and_3_out, comparator_1_gt, I_q_2[3]);
  Pull_Resistor pull_resistor_2 (.node(pull_resistor_2_node));
  assign pull_resistor_2_node = rom_1_data[16] ? or_1_out : 1'bz;  // Controlled_Buffer controlled_buffer_1
  LED led_16 (.in(pull_resistor_3_node[2]));
  LED led_17 (.in(pull_resistor_3_node[3]));
  LED led_18 (.in(pull_resistor_3_node[4]));
  LED led_19 (.in(pull_resistor_3_node[5]));
  Pull_Resistor pull_resistor_3 (.node(pull_resistor_3_node));
  RAM #(.addrWidth(4), .bus("separate")) ram_1 (
    .addr(pull_resistor_1_node), .data(pull_resistor_3_node), .str(rom_1_data[2]), .sel(ram_select_1_s1),
    .clk(and_6_out), .ld(pull_resistor_4_node));  // open: din, clr
  Pull_Resistor #(.pull(1)) pull_resistor_4 (.node(pull_resistor_4_node));
  LED led_20 (.in(I_q[0]));
  LED led_21 (.in(counter_1_q[0]));
  Step_reset step_reset_1 (.in_1(rom_1_data), .out_2(step_reset_1_out_2));
  D_Flip_Flop d_ff_1 (
    .clk(and_6_out), .D(pull_resistor_2_node), .Q(d_ff_1_q), .reset(and_4_out));  // open: Qn, preset, en
  and and_4 (and_4_out, not_2_out, and_6_out);
  not not_2 (not_2_out, rom_1_data[16]);
  LED led_22 (.in(pull_resistor_3_node[1]));
  LED led_23 (.in(pull_resistor_3_node[0]));
  Register I (.D(controlled_buffer_4_out), .Q({I_q_2, I_q}), .clk(and_6_out));  // open: en, clr
  Comparator comparator_1 (
    .a(A_q), .b(controlled_buffer_5_out), .gt(comparator_1_gt), .eq(comparator_1_eq), .lt(comparator_1_lt));
  assign pull_resistor_1_node = ram_select_1_en ? MA_q : 4'bz;  // Controlled_Buffer controlled_buffer_2
  Register #(.width(4)) MA (.D(controlled_buffer_3_out), .Q(MA_q), .clk(and_6_out));  // open: en, clr
  assign controlled_buffer_3_out = rom_1_data[5] ? controlled_buffer_5_out[3:0] : 4'bz;  // Controlled_Buffer controlled_buffer_3
  RAM #(.addrWidth(4), .bus("separate")) ram_2 (
    .addr(pull_resistor_1_node), .din(controlled_buffer_5_out), .data(pull_resistor_3_node),
    .str(rom_1_data[2]), .sel(ram_select_1_s0), .clk(and_6_out), .ld(pull_resistor_4_node));  // open: clr
  RAM_Select ram_select_1 (
    .II(rom_1_data[4]), .RO(or_2_out), .S1(ram_select_1_s1), .S0(ram_select_1_s0), .EN(ram_select_1_en));
  or or_2 (or_2_out, rom_1_data[2], rom_1_data[1]);
  assign controlled_buffer_4_out = rom_1_data[4] ? controlled_buffer_5_out : 8'bz;  // Controlled_Buffer controlled_buffer_4
  assign controlled_buffer_5_out = rom_1_data[3] ? {I_q_2, I_q} : 8'bz;  // Controlled_Buffer controlled_buffer_5
  ROM #(.addrWidth(7), .dataWidth(17)) rom_1 (.addr({I_q_2, counter_1_q}), .data(rom_1_data));  // open: sel
  LED led_24 (.in(controlled_buffer_5_out[7]));
  LED led_25 (.in(controlled_buffer_5_out[6]));
  assign controlled_buffer_5_out = rom_1_data[1] ? pull_resistor_3_node : 8'bz;  // Controlled_Buffer controlled_buffer_6
  Pull_Resistor pull_resistor_5 (.node(controlled_buffer_5_out[7]));
  Pull_Resistor pull_resistor_6 (.node(controlled_buffer_5_out[6]));
  LED led_26 (.in(controlled_buffer_5_out[2]));
  LED led_27 (.in(controlled_buffer_5_out[3]));
  LED led_28 (.in(controlled_buffer_5_out[5]));
  LED led_29 (.in(controlled_buffer_5_out[4]));
  Pull_Resistor pull_resistor_7 (.node(controlled_buffer_5_out[5]));
  Pull_Resistor pull_resistor_8 (.node(controlled_buffer_5_out[2]));
  Pull_Resistor pull_resistor_9 (.node(controlled_buffer_5_out[4]));
  Pull_Resistor pull_resistor_10 (.node(controlled_buffer_5_out[3]));
  LED led_30 (.in(controlled_buffer_5_out[0]));
  LED led_31 (.in(controlled_buffer_5_out[1]));
  Pull_Resistor pull_resistor_11 (.node(controlled_buffer_5_out[1]));
  Pull_Resistor pull_resistor_12 (.node(controlled_buffer_5_out[0]));
  LED led_32 (.in(rom_1_data[15]));
  LED led_33 (.in(rom_1_data[16]));
  assign controlled_buffer_5_out[3:0] = rom_1_data[7] ? PC_q : 4'bz;  // Controlled_Buffer controlled_buffer_7
  assign controlled_buffer_8_out = rom_1_data[6] ? controlled_buffer_5_out[3:0] : 4'bz;  // Controlled_Buffer controlled_buffer_8
  assign controlled_buffer_5_out = rom_1_data[9] ? A_q : 8'bz;  // Controlled_Buffer controlled_buffer_9
  Register A (.D(controlled_buffer_10_out), .Q(A_q), .clk(and_6_out));  // open: en, clr
  assign controlled_buffer_10_out = rom_1_data[10] ? controlled_buffer_5_out : 8'bz;  // Controlled_Buffer controlled_buffer_10
  Adder adder_1 (.a(A_q), .b(controlled_inverter_1_out), .out(adder_1_out), .cin(rom_1_data[12]));  // open: cout
  assign controlled_buffer_5_out = rom_1_data[11] ? SUM_q : 8'bz;  // Controlled_Buffer controlled_buffer_11
  assign controlled_buffer_12_out = rom_1_data[14] ? controlled_buffer_5_out : 8'bz;  // Controlled_Buffer controlled_buffer_12
  assign controlled_buffer_13_out = rom_1_data[15] ? controlled_buffer_5_out : 8'bz;  // Controlled_Buffer controlled_buffer_13
  LED led_34 (.in(rom_1_data[14]));
  LED led_35 (.in(rom_1_data[12]));
  LED led_36 (.in(rom_1_data[13]));
  LED led_37 (.in(rom_1_data[11]));
  Counter #(.width(4), .max('hf)) PC (
    .load(rom_1_data[6]), .D(controlled_buffer_8_out), .count(not_3_out), .Q(PC_q), .clk(and_5_out));  // open: carry, clr
  not not_3 (not_3_out, rom_1_data[6]);
  LED led_38 (.in(PC_q[3]));
  and and_5 (and_5_out, and_6_out, or_3_out);
  or or_3 (or_3_out, d_ff_1_q, rom_1_data[8]);
  Register SUM (.D(adder_1_out), .Q(SUM_q), .clk(not_4_out));  // open: en, clr
  not not_4 (not_4_out, and_6_out);
  assign controlled_inverter_1_out = rom_1_data[12] ? ~B_q : 8'bz;  // Controlled_Inverter controlled_inverter_1
  assign controlled_inverter_1_out = not_5_out ? B_q : 8'bz;  // Controlled_Buffer controlled_buffer_14
  not not_5 (not_5_out, rom_1_data[12]);
  assign controlled_buffer_5_out = rom_1_data[13] ? B_q : 8'bz;  // Controlled_Buffer controlled_buffer_15
  Register B (.D(controlled_buffer_12_out), .Q(B_q), .clk(and_6_out));  // open: en, clr
  Register OUT (.D(controlled_buffer_13_out), .Q(OUT_q), .clk(and_6_out));  // open: en, clr
  LED led_39 (.in(rom_1_data[10]));
  LED led_40 (.in(rom_1_data[9]));
  LED led_41 (.in(rom_1_data[7]));
  LED led_42 (.in(rom_1_data[8]));
  LED led_43 (.in(PC_q[2]));
  LED led_44 (.in(PC_q[1]));
  LED led_45 (.in(PC_q[0]));
  LED led_46 (.in(A_q[4]));
  LED led_47 (.in(A_q[7]));
  LED led_48 (.in(A_q[5]));
  LED led_49 (.in(A_q[6]));
  LED led_50 (.in(SUM_q[4]));
  LED led_51 (.in(SUM_q[6]));
  LED led_52 (.in(SUM_q[7]));
  LED led_53 (.in(SUM_q[5]));
  LED led_54 (.in(B_q[6]));
  LED led_55 (.in(B_q[5]));
  LED led_56 (.in(B_q[4]));
  LED led_57 (.in(B_q[7]));
  _7_Segment_Display u_7_segment_display_1 (.g(binary_to_bcd_1_negative));  // open: f, a, b, e, d, c, dp
  Binary_to_BCD binary_to_bcd_1 (
    .in_1(OUT_q), .UNITS(binary_to_bcd_1_units), .TENS(binary_to_bcd_1_tens),
    .HUNDREDS(binary_to_bcd_1_hundreds), .NEGATIVE(binary_to_bcd_1_negative), .in_2(in_1));
  LED led_58 (.in(rom_1_data[6]));
  LED led_59 (.in(rom_1_data[3]));
  LED led_60 (.in(rom_1_data[4]));
  LED led_61 (.in(rom_1_data[5]));
  LED led_62 (.in(A_q[2]));
  LED led_63 (.in(A_q[1]));
  LED led_64 (.in(A_q[3]));
  LED led_65 (.in(A_q[0]));
  LED led_66 (.in(SUM_q[1]));
  LED led_67 (.in(SUM_q[3]));
  LED led_68 (.in(SUM_q[2]));
  LED led_69 (.in(SUM_q[0]));
  LED led_70 (.in(B_q[2]));
  LED led_71 (.in(B_q[1]));
  LED led_72 (.in(B_q[0]));
  LED led_73 (.in(B_q[3]));
  Hex_Digit_Display hex_digit_display_1 (.value(binary_to_bcd_1_tens));  // open: dp
  Hex_Digit_Display hex_digit_display_2 (.value(binary_to_bcd_1_hundreds));  // open: dp
  LED led_74 (.in(rom_1_data[0]));
  LED led_75 (.in(rom_1_data[2]));
  LED led_76 (.in(rom_1_data[1]));
  Hex_Digit_Display hex_digit_display_3 (.value(binary_to_bcd_1_units));  // open: dp
  and and_6 (and_6_out, not_6_out, clock_1_out);
  not not_6 (not_6_out, rom_1_data[0]);
  Clock clock_1 (.out(clock_1_out));

  // Notes on the sheet:
  //   contents of rom_1 (hex, n*v repeats v):
  //   a0 112 6*0 a0 112 28 402 4*0 a0 112 28 4002 4*0 a0 112 28 204 4*0 a0 112 28 2004 4*0 a0 112 28 4002
  //   c00 0 0 0 a0 112 28 5002 1c00 0 0 0 a0 112 8200 5*0 a0 112 148 5*0 a0 112 12000 48 4*0 a0 112 12000
  //   48 12*0 a0 112 12000 48 12*0 a0 112 c560 5*0 a0 112 1
  //   OI
  //   CP
  //   SU
  //   BI
  //   EO
  //   BO
  //   CE
  //   CO
  //   AO
  //   AI
  //   IO
  //   J
  //   MI
  //   II
  //   RO
  //   RI
  //   H
endmodule

module Step_reset (
  input  [16:0] in_1,
  output out_2
);

  wire not_1_out, not_2_out, not_3_out, not_4_out, not_5_out, not_6_out, not_7_out, not_8_out, not_9_out,
       not_10_out, not_11_out, not_12_out, not_13_out, not_14_out, not_15_out, not_16_out, not_17_out,
       undriven;

  not not_1 (not_1_out, in_1[0]);
  not not_2 (not_2_out, in_1[1]);
  not not_3 (not_3_out, in_1[2]);
  not not_4 (not_4_out, in_1[3]);
  not not_5 (not_5_out, in_1[4]);
  not not_6 (not_6_out, in_1[5]);
  not not_7 (not_7_out, in_1[6]);
  not not_8 (not_8_out, in_1[7]);
  not not_9 (not_9_out, in_1[8]);
  not not_10 (not_10_out, in_1[9]);
  not not_11 (not_11_out, in_1[10]);
  not not_12 (not_12_out, in_1[11]);
  not not_13 (not_13_out, in_1[12]);
  not not_14 (not_14_out, in_1[13]);
  not not_15 (not_15_out, in_1[14]);
  not not_16 (not_16_out, in_1[15]);
  not not_17 (not_17_out, in_1[16]);
  // NOT_Gate not_18 has open pins: in=undriven, out=open
  and and_1 (out_2, not_1_out, not_2_out, not_3_out, not_4_out, not_5_out, not_6_out, not_7_out, not_8_out, not_9_out, not_11_out, not_12_out, not_13_out, not_14_out, not_15_out, not_16_out, not_17_out);
endmodule

module ADD3 (
  input  A3,
  input  A2,
  input  A1,
  input  A0,
  output S3,
  output S2,
  output S1,
  output S0
);

  wire and_1_out, and_2_out, and_3_out, and_4_out, and_5_out, and_6_out, and_7_out, and_8_out, and_9_out,
       and_10_out, not_1_out, not_2_out, not_3_out, not_4_out, not_5_out, not_6_out, not_7_out, not_8_out;

  and and_1 (and_1_out, A2, A0);
  and and_2 (and_2_out, A2, A1);
  and and_3 (and_3_out, A2, not_1_out, not_2_out);
  not not_1 (not_1_out, A1);
  not not_2 (not_2_out, A0);
  and and_4 (and_4_out, A3, A0);
  not not_3 (not_3_out, A2);
  and and_5 (and_5_out, not_3_out, A1);
  and and_6 (and_6_out, A1, A0);
  and and_7 (and_7_out, A3, not_4_out);
  not not_4 (not_4_out, A0);
  not not_5 (not_5_out, A3);
  not not_6 (not_6_out, A2);
  and and_8 (and_8_out, not_5_out, not_6_out, A0);
  and and_9 (and_9_out, A2, A1, not_7_out);
  not not_7 (not_7_out, A0);
  and and_10 (and_10_out, A3, not_8_out);
  not not_8 (not_8_out, A0);
  or or_1 (S3, and_1_out, and_2_out, A3);
  or or_2 (S2, and_3_out, and_4_out);
  or or_3 (S1, and_5_out, and_6_out, and_7_out);
  or or_4 (S0, and_8_out, and_9_out, and_10_out);
endmodule

module Binary_to_BCD (
  input  [7:0] in_1,
  input  in_2,
  output [3:0] UNITS,
  output [3:0] TENS,
  output [3:0] HUNDREDS,
  output NEGATIVE
);

  wire add3_1_s0, add3_1_s1, add3_1_s2, add3_1_s3, add3_2_s0, add3_2_s1, add3_2_s2, add3_2_s3, add3_3_s0,
       add3_3_s1, add3_3_s2, add3_3_s3, add3_5_s0, add3_5_s1, add3_5_s2, add3_5_s3, add3_7_s0, add3_7_s1,
       add3_7_s2, and_2_out, not_1_out, not_3_out;
  wire [6:0] not_2_out, subtractor_1_out;
  wire [6:1] controlled_buffer_1_out;

  and and_1 (NEGATIVE, in_1[7], in_2);
  not not_1 (not_1_out, in_2);
  assign {controlled_buffer_1_out, UNITS[0]} = NEGATIVE ? not_2_out : 7'bz;  // Controlled_Buffer controlled_buffer_1
  Subtractor #(.width(7)) subtractor_1 (.a(in_1[6:0]), .b(7'b0000001), .out(subtractor_1_out));  // open: bin, bout
  assign not_2_out = ~subtractor_1_out;  // NOT_Gate not_2, 7 bits wide
  and and_2 (and_2_out, in_1[7], not_1_out);
  assign {controlled_buffer_1_out, UNITS[0]} = not_3_out ? in_1[6:0] : 7'bz;  // Controlled_Buffer controlled_buffer_2
  not not_3 (not_3_out, NEGATIVE);
  ADD3 add3_1 (
    .A3(HUNDREDS[3]), .A2(and_2_out), .A1(controlled_buffer_1_out[6]), .A0(controlled_buffer_1_out[5]),
    .S3(add3_1_s3), .S2(add3_1_s2), .S1(add3_1_s1), .S0(add3_1_s0));
  Pull_Resistor pull_resistor_1 (.node(HUNDREDS[3]));
  ADD3 add3_2 (
    .A3(add3_3_s2), .A2(add3_3_s1), .A1(add3_3_s0), .A0(controlled_buffer_1_out[3]), .S3(add3_2_s3),
    .S2(add3_2_s2), .S1(add3_2_s1), .S0(add3_2_s0));
  ADD3 add3_3 (
    .A3(add3_1_s2), .A2(add3_1_s1), .A1(add3_1_s0), .A0(controlled_buffer_1_out[4]), .S3(add3_3_s3),
    .S2(add3_3_s2), .S1(add3_3_s1), .S0(add3_3_s0));
  ADD3 add3_4 (
    .A3(add3_5_s2), .A2(add3_5_s1), .A1(add3_5_s0), .A0(controlled_buffer_1_out[1]), .S3(TENS[0]),
    .S2(UNITS[3]), .S1(UNITS[2]), .S0(UNITS[1]));
  ADD3 add3_5 (
    .A3(add3_2_s2), .A2(add3_2_s1), .A1(add3_2_s0), .A0(controlled_buffer_1_out[2]), .S3(add3_5_s3),
    .S2(add3_5_s2), .S1(add3_5_s1), .S0(add3_5_s0));
  ADD3 add3_6 (
    .A3(add3_7_s2), .A2(add3_7_s1), .A1(add3_7_s0), .A0(add3_5_s3), .S3(HUNDREDS[0]), .S2(TENS[3]),
    .S1(TENS[2]), .S0(TENS[1]));
  ADD3 add3_7 (
    .A3(HUNDREDS[3]), .A2(add3_1_s3), .A1(add3_3_s3), .A0(add3_2_s3), .S3(HUNDREDS[1]), .S2(add3_7_s2),
    .S1(add3_7_s1), .S0(add3_7_s0));

  assign HUNDREDS[2] = HUNDREDS[3];
endmodule

module RAM_Select (
  input  II,
  input  RO,
  output S1,
  output EN,
  output S0
);

  wire not_1_out;

  and and_1 (S1, II, RO);
  not not_1 (not_1_out, II);
  and and_2 (S0, not_1_out, RO);
  or or_1 (EN, S1, S0);
endmodule
